# Fritzing sketch LR_Meter (saved by Fritzing 0.9.3b)
circuit board: 8.46667cm x 5.64444cm
breadboards: 1

parts:
  Part1 = Arduino Nano (Rev3.0)
  Part2 = Thumb Joystick
  R2 = Resistor [tolerance=±5% resistance=2k package=THT]
  R3 = Resistor [tolerance=±5% resistance=20k package=THT]
  R4 = Resistor [tolerance=±5% resistance=220k package=THT]
  R5 = Resistor [tolerance=±5% resistance=1M package=THT]
  J1 = Screw terminal - 2 pins [package=THT]
  C1 = Capacitor [package=cap-pth-small2]
  C2 = Capacitor [package=cap-pth-small2]
  J3 = Screw terminal - 2 pins [package=THT]
  U1 = LM393 [package=so08]
  R1 = Resistor [tolerance=±5% resistance=1k package=THT]
  R6 = Resistor [tolerance=±5% resistance=150 package=THT]
  R7 = Resistor [tolerance=±5% resistance=330 package=THT]  # not connected
  D1 = Diode [package=diode-1n4148]

nets:
  GND: Part1.GND, Part2.GND, C1.2, C2.1, J3.pin1, J3.pin2, U1.G1_-IN, U1.G1_+IN, U1.G1_V-, R1.Pin_1
  N1: Part1.D2, Part2.SEL, R1.Pin_0
  N2: Part1.D7, J1.pin2
  N3: Part1.D8, R3.Pin_0
  N4: Part1.D9, R4.Pin_0
  N5: Part1.D10, R5.Pin_0
  N6: Part1.D12/MISO, U1.G1_OUT
  5V: Part1.5V, Part2.VCC, U1.G1_V+
  N7: Part1.A2, R2.Pin_1, R3.Pin_1, R4.Pin_1, R5.Pin_1, J1.pin1
  N8: Part1.A1, Part2.HORZ
  N9: Part1.A0, Part2.VERT
  N10: Part1.D13/SCK, R6.Pin_0
  N11: C1.1, C2.2, D1.C

notes:
  resistance Terminal
